# Fritzing sketch sensor (saved by Fritzing 1.0.6)
breadboards: 1

parts:
  A1 = ESP32-C6 devkit
  A2 = DHT22 module
  Sensor1 = MQ-xx breakout
  A3 = Sim900a module
  OLED1 = OLED 128x64 I2C Monochrome Display VDD-GND
  R1 = Resistor [tolerance=±5% resistance=1k package="0603 [SMD]"]
  R2 = Resistor [tolerance=±5% resistance=1k package="0603 [SMD]"]

nets:
  GND: A1.Pin_1, A1.Pin_17, A1.Pin_30, A2.-, Sensor1.GND, A3.Pin_1, A3.Pin_8, A3.Pin_12, OLED1.GND, R2.Pin_0
  N1: A1.Pin_2, A2.+, OLED1.VDD
  N2: A1.Pin_4, A2.Out
  N3: A1.Pin_6, OLED1.SDA
  N4: A1.Pin_7, OLED1.SCK
  N5: A1.Pin_8, R1.Pin_0, R2.Pin_1
  N6: A1.Pin_15, A1.Pin_16, Sensor1.VCC, A3.Pin_15
  N7: A1.Pin_19, A3.Pin_10
  N8: A1.Pin_20, A3.Pin_13
  N9: Sensor1.AO, R1.Pin_1

custom parts:
  ESP32-C6 devkit: ESP32 / ESP32-C6 WiFi+Bluetooth Internet Of Things Dual Type-C Development Board Core Board ESP32-C6-DevKit.
  DHT22 module: DHT22 module. Pins VCC Data GND.
  MQ-xx breakout: MQ-xx gas sensor
  Sim900a module: SIM900A GSM module delivers GSM/GPRS 900/1800MHz performance for voice, SMS, Data, and Fax in a small form factor and with low power consumption.
  OLED 128x64 I2C Monochrome Display VDD-GND: OLED 128x64 I2C Monochrome Display. Note: there are two variants of this part, this one is the VDD GND SCK SDA variant. The other is GND VDD SCK SDA. Make sure you select the part that matches your module as using the incorrect part will probably destroy your module! In addition the mounting holes are marked on silkscreen but not by default drilled. If you want drilled mounting holes, copy a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
